# Fritzing sketch nPID (saved by Fritzing 0.9.0b)

parts:
  Part1 = Arduino Mega ADK (Rev3)  # not connected
  Part2 = Arduino Prototyping Shield
  Rotary_Encoder = Rotary Encoder [package=THT]
  LCD1 = LCD screen
  PushButton = Pushbutton [package="[THT]"]
  R1 = Trimmer Potentiometer [maximum_resistance=10kΩ package=THT]
  R2 = Resistor [tolerance=±5% resistance=470 package=THT]
  T3 = Maxim (Dallas) OneWire DS18B20 Digital Temperature Sensor [package="TO92 [THT]"]
  DS18B20 = Maxim (Dallas) OneWire DS18B20 Digital Temperature Sensor [package="TO92 [THT]"]

nets:
  N1: Part2.D4, LCD1.DB3, LCD1.DB4
  N2: Part2.D8, LCD1.E
  N3: Part2.D9, LCD1.RS
  N4: Part2.D2, Rotary_Encoder.EncoderPinB
  N5: Part2.D3, Rotary_Encoder.EncoderPinA
  N6: Part2.D5, LCD1.DB5
  N7: Part2.D6, LCD1.DB6
  N8: Part2.D7, LCD1.DB7
  N9: Part2.A0, PushButton.Pin_1, PushButton.Pin_2
  N10: Part2.A1, Part2.N$362
  N11: Part2.+5V, Part2.N$58
  N12: Part2.GND, Part2.N$376
  N13: Part2.N$47, DS18B20.GND
  N14: Part2.N$59, T3.GND
  N15: Part2.N$69, T3.Vout
  N16: Part2.N$70, LCD1.LED+
  N17: Part2.N$71, LCD1.VDD
  N18: Part2.N$231, Part2.N$279, R1.leg1
  N19: Part2.N$234, Part2.N$317, R1.leg2
  N20: Part2.N$245, LCD1.V0, R1.wiper
  N21: Part2.N$284, R2.Pin_0
  N22: Part2.N$296, LCD1.VSS, LCD1.R/W
  N23: Part2.N$318, LCD1.LED-
  N24: Part2.N$320, PushButton.Pin_4
  N25: Part2.N$361, DS18B20.Vout
  N26: Part2.N$363, R2.Pin_1
  N27: Part2.N$377, T3.+Vs
  N28: Part2.N$378, DS18B20.+Vs
  N29: Part2.N$381, Rotary_Encoder.EncoderPinC

notes:
  To Relay Board ==>
  -Relay 1
  -Relay 2
  -Vcc +5V
  -Ground
