# Fritzing sketch power (saved by Fritzing 0.9.0b)

parts:
  U1 = Power Outlet [chip_label=IC package="SIP (Single Inline) [THT]"]
  U2 = Power Outlet [chip_label=IC package="SIP (Single Inline) [THT]"]
  U3 = Power Outlet [chip_label=IC package="SIP (Single Inline) [THT]"]

nets:
  N1: U1.ground, U2.ground, U3.ground

notes:
  to power outlet (120v AC)
  - neutral
  - hot
  - ground
  to cool relay -
  to heat relay -
  cooling
  mains power
  arduino/fans
  heating

custom parts:
  Power Outlet: A standard power outlet. Silver screws are neutral, brass screws are hot. Green screw is ground.
  Power Outlet: A standard power outlet. Silver screws are neutral, brass screws are hot. Green screw is ground.
